// Logisim project dff.circ as structural Verilog: 1 circuit, main circuit main
module main (
);

  wire and_1_out, and_2_out, clock_1_out, D_out, Enable_out, nand_1_out, nand_2_out, nand_3_out, nand_4_out,
       nand_5_out, not_1_out, Resey_out;

  Button D (.out(D_out));
  Clock clock_1 (.out(clock_1_out));
  Button Enable (.out(Enable_out));
  and and_1 (and_1_out, clock_1_out, Enable_out);
  not not_1 (not_1_out, D_out);
  D_Flip_Flop d_ff_1 ();  // open: clk, D, Q, Qn, preset, en, reset
  nand nand_1 (nand_1_out, D_out, and_1_out);
  nand nand_2 (nand_2_out, not_1_out, and_1_out);
  nand nand_3 (nand_3_out, nand_1_out, nand_4_out);
  nand nand_4 (nand_4_out, nand_3_out, nand_2_out);
  Button Resey (.out(Resey_out));
  and and_2 (and_2_out, nand_3_out, Resey_out);
  nand nand_5 (nand_5_out, nand_3_out, Resey_out);
  LED Q (.in(and_2_out));
  LED nQ (.in(nand_5_out));
endmodule
