// Logisim project dff_positive_rise.circ as structural Verilog: 1 circuit, main circuit main
module main (
);

  wire and_1_out, Clc_out, Data_out, Enable_out, nand_1_out, nand_2_out, nand_3_out, nand_4_out, nand_5_out,
       nand_6_out, Reset_out;

  Clock Clc (.out(Clc_out));
  Button Enable (.out(Enable_out));
  Button Data (.out(Data_out));
  and and_1 (and_1_out, Clc_out, Enable_out);
  nand nand_1 (nand_1_out, nand_2_out, nand_4_out);
  nand nand_2 (nand_2_out, nand_1_out, Reset_out, and_1_out);
  nand nand_3 (nand_3_out, and_1_out, nand_2_out, nand_4_out);
  nand nand_4 (nand_4_out, nand_3_out, Reset_out, Data_out);
  Button Reset (.out(Reset_out));
  nand nand_5 (nand_5_out, nand_2_out, nand_6_out);
  LED Q (.in(nand_5_out));
  LED nQ (.in(nand_6_out));
  nand nand_6 (nand_6_out, nand_3_out, Reset_out, nand_5_out);
endmodule
